// Logisim project riscv_pip_dp .circ as structural Verilog: 9 circuits, main circuit pc
module main (
);

  wire alu_src, branch, jr, less, main_contrl_cu_aluc_bc_1_out_10, main_contrl_cu_aluc_bc_1_ujj_4,
       main_contrl_cu_aluc_bc_1_ujj_5, main_contrl_cu_aluc_bc_1_ujj_7, main_contrl_cu_aluc_bc_1_ujj_8,
       mem_reg_2, mem_write, pc_sel, reg_write, register_7_q, register_8_q, register_13_q, register_17_q,
       register_21_q, zero;
  wire [1:0] Forword_A, Forword_B, mem_reg_1_0;
  wire [2:0] main_contrl_cu_aluc_bc_1_ujj_6, mem_reg, register_9_q, register_19_q;
  wire [3:0] alu_ctlr, main_contrl_cu_aluc_bc_1_ujj_9;
  wire [4:0] RD_2_q, RD_3_q, RD_q;
  wire [31:0] adder_3_out, alu2_1_ujj_6, current_pc, data_mem_1_ujj_4, imm_gen_1_ujj_2,
       instruction_mem_1_ujj_2, multiplexer_1_out, multiplexer_2_out, multiplexer_3_out, multiplexer_4_out,
       multiplexer_5_out, multiplexer_6_out, multiplexer_7_out, pc_1_ujj_2, pc_4, pc_offset,
       reg_file_1_ujj_6, reg_file_1_ujj_7, register_1_q, register_2_q, register_3_q, register_4_q,
       register_5_q, register_6_q, register_14_q, register_15_q, register_16_q, register_23_q;

  pc pc_1 (.ujj(multiplexer_6_out), .ujj_2(pc_1_ujj_2));
  main_contrl_Cu_Aluc_Bc main_contrl_cu_aluc_bc_1 (
    .ujj(register_2_q), .ujj_4(main_contrl_cu_aluc_bc_1_ujj_4), .ujj_5(main_contrl_cu_aluc_bc_1_ujj_5),
    .ujj_6(main_contrl_cu_aluc_bc_1_ujj_6), .ujj_7(main_contrl_cu_aluc_bc_1_ujj_7),
    .ujj_8(main_contrl_cu_aluc_bc_1_ujj_8), .ujj_9(main_contrl_cu_aluc_bc_1_ujj_9), .ujj_2(zero),
    .ujj_3(less), .out_10(main_contrl_cu_aluc_bc_1_out_10));
  instruction_mem instruction_mem_1 (.ujj(pc_1_ujj_2), .ujj_2(instruction_mem_1_ujj_2));
  Adder #(.width(32)) adder_1 (.a(current_pc), .b(32'h4), .out(pc_4));  // open: cin, cout
  Adder #(.width(32)) adder_2 (.a(current_pc), .b(register_6_q));  // open: out, cin, cout
  Register #(.width(32)) register_1 (.D(pc_1_ujj_2), .Q(register_1_q));  // open: en, clk, clr
  Register #(.width(32)) register_2 (.D(instruction_mem_1_ujj_2), .Q(register_2_q));  // open: en, clk, clr
  imm_gen imm_gen_1 (.ujj(register_2_q), .ujj_2(imm_gen_1_ujj_2));
  Reg_file reg_file_1 (
    .ujj(reg_write), .ujj_6(reg_file_1_ujj_6), .ujj_2(register_2_q[4:0]), .ujj_3(register_2_q[9:5]),
    .ujj_7(reg_file_1_ujj_7), .ujj_4(RD_3_q), .ujj_5(multiplexer_7_out));
  Register #(.width(32)) register_3 (.D(reg_file_1_ujj_7), .Q(register_3_q));  // open: en, clk, clr
  Register #(.width(32)) register_4 (.D(register_1_q), .Q(register_4_q));  // open: en, clk, clr
  Register #(.width(32)) register_5 (.D(reg_file_1_ujj_6), .Q(register_5_q));  // open: en, clk, clr
  Multiplexer #(.select(2), .width(32), .enable("false")) multiplexer_1 (
    .in0(register_3_q), .in1(multiplexer_7_out), .in2(register_16_q), .out(multiplexer_1_out), .sel(Forword_B));  // open: in3
  Register #(.width(32)) register_6 (.D(imm_gen_1_ujj_2), .Q(register_6_q));  // open: en, clk, clr
  Register #(.width(5)) RD (.D(register_2_q[14:10]), .Q(RD_q));  // open: en, clk, clr
  Register #(.width(1)) register_7 (.D(main_contrl_cu_aluc_bc_1_ujj_4), .Q(register_7_q));  // open: en, clk, clr
  Register #(.width(1)) register_8 (.D(main_contrl_cu_aluc_bc_1_ujj_5), .Q(register_8_q));  // open: en, clk, clr
  Register #(.width(3)) register_9 (
    .D(main_contrl_cu_aluc_bc_1_ujj_6), .Q(register_9_q), .clk(main_contrl_cu_aluc_bc_1_ujj_8),
    .clr(main_contrl_cu_aluc_bc_1_ujj_8));  // open: en
  Register #(.width(1)) register_10 (
    .D(main_contrl_cu_aluc_bc_1_ujj_8), .Q(reg_write), .clk(alu_src), .clr(alu_src));  // open: en
  Register #(.width(1)) register_11 (.D(main_contrl_cu_aluc_bc_1_ujj_7), .Q(alu_src));  // open: en, clk, clr
  Register #(.width(4)) register_12 (.D(main_contrl_cu_aluc_bc_1_ujj_9), .Q(alu_ctlr));  // open: en, clk, clr
  Register #(.width(1)) register_13 (.D(main_contrl_cu_aluc_bc_1_out_10), .Q(register_13_q));  // open: en, clk, clr
  Forword_Cont forword_cont_1 (
    .ujj(register_2_q[4:0]), .ujj_5(Forword_A), .ujj_2(register_2_q[9:5]), .ujj_3(RD_q), .ujj_6(Forword_B),
    .ujj_4(RD_2_q));
  Multiplexer #(.select(2), .width(32), .enable("false")) multiplexer_2 (
    .in0(register_5_q), .in1(multiplexer_7_out), .in2(register_16_q), .out(multiplexer_2_out), .sel(Forword_A));  // open: in3
  Multiplexer #(.width(32), .enable("false")) multiplexer_3 (
    .in0(multiplexer_1_out), .in1(register_6_q), .out(multiplexer_3_out), .sel(alu_src));
  ALU2 alu2_1 (
    .ujj_4(zero), .ujj_5(less), .ujj_2(multiplexer_3_out), .ujj_6(alu2_1_ujj_6), .ujj_3(alu_ctlr));  // open: ujj
  Register #(.width(32)) register_14 (.D(multiplexer_1_out), .Q(register_14_q));  // open: en, clk, clr
  Register #(.width(32)) register_15 (.D(register_4_q), .Q(register_15_q));  // open: en, clk, clr
  Register #(.width(32)) register_16 (.D(alu2_1_ujj_6), .Q(register_16_q));  // open: en, clk, clr
  Register #(.width(5)) RD_2 (.D(RD_q), .Q(RD_2_q));  // open: en, clk, clr
  Register #(.width(1)) register_17 (.D(register_7_q), .Q(register_17_q));  // open: en, clk, clr
  Register #(.width(1)) register_18 (.D(register_8_q), .Q(mem_write));  // open: en, clk, clr
  Register #(.width(3)) register_19 (.D(register_9_q), .Q(register_19_q));  // open: en, clk, clr
  Register #(.width(1)) register_20 (.D(reg_write), .Q(reg_write));  // open: en, clk, clr
  Register #(.width(1)) register_21 (.D(register_13_q), .Q(register_21_q));  // open: en, clk, clr
  Register #(.width(32)) register_22 (.D(register_15_q), .Q(current_pc));  // open: en, clk, clr
  data_mem data_mem_1 (.ujj(register_14_q), .ujj_4(data_mem_1_ujj_4), .ujj_2(register_16_q), .ujj_3(mem_write));
  Register #(.width(32)) register_23 (.D(data_mem_1_ujj_4), .Q(register_23_q));  // open: en, clk, clr
  Register #(.width(5)) RD_3 (.D(RD_2_q), .Q(RD_3_q));  // open: en, clk, clr
  Register #(.width(1)) register_24 (.D(register_17_q), .Q(branch));  // open: en, clk, clr
  Register #(.width(3)) register_25 (.D(register_19_q), .Q(mem_reg));  // open: en, clk, clr
  Register #(.width(1)) register_26 (.D(reg_write), .Q(reg_write));  // open: en, clk, clr
  Register #(.width(1)) register_27 (.D(register_21_q), .Q(pc_sel));  // open: en, clk, clr
  Adder #(.width(32)) adder_3 (.a(register_5_q), .b(register_6_q), .out(adder_3_out));  // open: cin, cout
  Multiplexer #(.width(32), .enable("false")) multiplexer_4 (
    .in0(pc_4), .in1(pc_offset), .out(multiplexer_4_out), .sel(pc_sel));
  Multiplexer #(.select(2), .width(32), .enable("false")) multiplexer_5 (
    .in0(pc_4), .in1(pc_offset), .in2(register_16_q), .in3(register_23_q), .out(multiplexer_5_out),
    .sel(mem_reg_1_0));
  Multiplexer #(.width(32), .enable("false")) multiplexer_6 (
    .in0(multiplexer_4_out), .in1(adder_3_out), .out(multiplexer_6_out), .sel(jr));
  Multiplexer #(.width(32), .enable("false")) multiplexer_7 (
    .in0(multiplexer_5_out), .in1(register_6_q), .out(multiplexer_7_out), .sel(mem_reg_2));

  // Notes on the sheet:
  //   Rs+imm
endmodule

module pc (
  input  [31:0] ujj,
  output [31:0] ujj_2
);
endmodule

module instruction_mem (
  input  [31:0] ujj,
  output [31:0] ujj_2
);
endmodule

module Reg_file (
  input  ujj,
  input  [4:0] ujj_2,
  input  [4:0] ujj_3,
  input  [4:0] ujj_4,
  input  [31:0] ujj_5,
  output [31:0] ujj_6,
  output [31:0] ujj_7
);
endmodule

module data_mem (
  input  [31:0] ujj,
  input  [31:0] ujj_2,
  input  ujj_3,
  output [31:0] ujj_4
);
endmodule

module imm_gen (
  input  [31:0] ujj,
  output [31:0] ujj_2
);
endmodule

module ALU2 (
  input  [31:0] ujj,
  input  [31:0] ujj_2,
  input  [3:0] ujj_3,
  output ujj_4,
  output ujj_5,
  output [31:0] ujj_6
);
endmodule

module main_contrl_Cu_Aluc_Bc (
  input  [31:0] ujj,
  input  ujj_2,
  input  ujj_3,
  output ujj_4,
  output ujj_5,
  output [2:0] ujj_6,
  output ujj_7,
  output ujj_8,
  output [3:0] ujj_9,
  output out_10
);
endmodule

module Forword_Cont (
  input  [4:0] ujj,
  input  [4:0] ujj_2,
  input  [4:0] ujj_3,
  input  [4:0] ujj_4,
  output [1:0] ujj_5,
  output [1:0] ujj_6
);
endmodule
