// Logisim project riscv_sc_dp.circ as structural Verilog: 9 circuits, main circuit main
module main (
);

  wire alu_src, branch, jr, less, mem_reg_2, mem_write, pc_sel, reg_write, zero;
  wire [1:0] mem_reg_1_0;
  wire [2:0] mem_reg;
  wire [3:0] alu_ctlr;
  wire [31:0] adder_3_out, alu2_1_ujj_6, branch_p1, data_mem_1_ujj_4, imm_gen_1_ujj_2, multiplexer_1_out,
       multiplexer_2_out, multiplexer_3_out, multiplexer_4_out, multiplexer_5_out, pc_1_ujj_2, pc_4,
       pc_offset, reg_file_1_ujj_6, reg_file_1_ujj_7;

  // main_contrl_Cu_Aluc_Bc branch: pin names not known; wires that end beside it: branch_p1, zero, less, branch, mem_write, mem_reg, alu_src, reg_write, alu_ctlr, pc_sel
  pc pc_1 (.ujj(multiplexer_4_out), .ujj_2(pc_1_ujj_2));
  instruction_mem instruction_mem_1 (.ujj(pc_1_ujj_2), .ujj_2(branch_p1));
  Adder #(.width(32)) adder_1 (.a(pc_1_ujj_2), .b(32'h4), .out(pc_4));  // open: cin, cout
  Adder #(.width(32)) adder_2 (.a(pc_1_ujj_2), .b(imm_gen_1_ujj_2), .out(pc_offset));  // open: cin, cout
  imm_gen imm_gen_1 (.ujj(branch_p1), .ujj_2(imm_gen_1_ujj_2));
  Reg_file reg_file_1 (
    .ujj(reg_write), .ujj_6(reg_file_1_ujj_6), .ujj_2(branch_p1[4:0]), .ujj_3(branch_p1[4:0]),
    .ujj_7(reg_file_1_ujj_7), .ujj_4(branch_p1[4:0]), .ujj_5(multiplexer_5_out));
  Multiplexer #(.width(32), .enable("false")) multiplexer_1 (
    .in0(reg_file_1_ujj_7), .in1(imm_gen_1_ujj_2), .out(multiplexer_1_out), .sel(alu_src));
  ALU2 alu2_1 (
    .ujj_4(zero), .ujj(reg_file_1_ujj_6), .ujj_5(less), .ujj_2(multiplexer_1_out), .ujj_6(alu2_1_ujj_6),
    .ujj_3(alu_ctlr));
  data_mem data_mem_1 (.ujj_4(data_mem_1_ujj_4), .ujj_2(alu2_1_ujj_6), .ujj_3(mem_write));  // open: ujj
  Multiplexer #(.width(32), .enable("false")) multiplexer_2 (
    .in0(pc_4), .in1(pc_offset), .out(multiplexer_2_out), .sel(pc_sel));
  Adder #(.width(32)) adder_3 (.a(reg_file_1_ujj_6), .b(imm_gen_1_ujj_2), .out(adder_3_out));  // open: cin, cout
  Multiplexer #(.select(2), .width(32), .enable("false")) multiplexer_3 (
    .in0(pc_4), .in1(pc_offset), .in2(alu2_1_ujj_6), .in3(data_mem_1_ujj_4), .out(multiplexer_3_out),
    .sel(mem_reg_1_0));
  Multiplexer #(.width(32), .enable("false")) multiplexer_4 (
    .in0(multiplexer_2_out), .in1(adder_3_out), .out(multiplexer_4_out), .sel(jr));
  Multiplexer #(.width(32), .enable("false")) multiplexer_5 (
    .in0(multiplexer_3_out), .in1(imm_gen_1_ujj_2), .out(multiplexer_5_out), .sel(mem_reg_2));

  // Notes on the sheet:
  //   Rs+imm
endmodule

module pc (
  input  [31:0] ujj,
  output [31:0] ujj_2
);
endmodule

module instruction_mem (
  input  [31:0] ujj,
  output [31:0] ujj_2
);
endmodule

module ALU (
  input  [31:0] ujj,
  input  [31:0] ujj_2,
  input  [2:0] ujj_3,
  output ujj_4,
  output ujj_5,
  output [31:0] ujj_6
);
endmodule

module Reg_file (
  input  ujj,
  input  [4:0] ujj_2,
  input  [4:0] ujj_3,
  input  [4:0] ujj_4,
  input  [31:0] ujj_5,
  output [31:0] ujj_6,
  output [31:0] ujj_7
);
endmodule

module data_mem (
  input  [31:0] ujj,
  input  [31:0] ujj_2,
  input  ujj_3,
  output [31:0] ujj_4
);
endmodule

module imm_gen (
  input  [31:0] ujj,
  output [31:0] ujj_2
);
endmodule

module ALU2 (
  input  [31:0] ujj,
  input  [31:0] ujj_2,
  input  [3:0] ujj_3,
  output ujj_4,
  output ujj_5,
  output [31:0] ujj_6
);
endmodule

module main_contrl_Cu_Aluc_Bc (
  input  [31:0] ujj,
  input  ujj_2,
  input  ujj_3,
  output ujj_4,
  output ujj_5,
  output [2:0] ujj_6,
  output ujj_7,
  output ujj_8,
  output [3:0] ujj_9,
  output out_10
);
endmodule
